# Fritzing sketch connexionat emces_apagat un pin (saved by Fritzing 0.9.5d)
breadboards: 1

parts:
  Raspberry_Pi_1 = Raspberry Pi 3 [part_number=RPI-3-V1.2]
  S1 = Momentary Switch [package=ksa_sealed_tac_switch]

nets:
  N1: Raspberry_Pi_1.GPIO3, S1.1
  N2: Raspberry_Pi_1.GND, S1.3

notes:
  GPIO3
  encendido
