# Fritzing sketch connexionat management (saved by Fritzing 0.9.5d)
breadboards: 1

parts:
  LCD1 = LCD screen
  RE1 = Rotary Encoder [package=THT]
  J1 = Piezo Speaker
  Raspberry_Pi_1 = Raspberry Pi 3 [part_number=RPI-3-V1.2]
  R1 = Rotary Potentiometer (Large) [maximum_resistance=100kΩ package=THT]
  U1 = ESP8266 NodeMCU LoLin module

nets:
  N1: LCD1.VSS, R1.leg1
  VDD: LCD1.VDD, LCD1.LED+, Raspberry_Pi_1.5V
  N2: LCD1.V0, R1.wiper
  N3: LCD1.RS, Raspberry_Pi_1.GIPO23
  GND: LCD1.R/W, LCD1.LED-, J1.pin1, Raspberry_Pi_1.GND, R1.leg2, U1.GND
  N4: LCD1.E, Raspberry_Pi_1.GIPO24
  N5: LCD1.DB4, Raspberry_Pi_1.GIPO26
  N6: LCD1.DB5, Raspberry_Pi_1.GIPO19
  N7: LCD1.DB6, Raspberry_Pi_1.GIPO13
  N8: LCD1.DB7, Raspberry_Pi_1.GIPO6
  N9: RE1.EncoderPinA, Raspberry_Pi_1.GIPO20
  N10: RE1.EncoderPinC, Raspberry_Pi_1.GIPO16
  N11: J1.pin2, Raspberry_Pi_1.GIPO18
  3V3: Raspberry_Pi_1.3v3, U1.Vin
  N12: Raspberry_Pi_1.GPIO3, U1.D1
  N13: Raspberry_Pi_1.GIPO4, U1.D2

custom parts:
  ESP8266 NodeMCU LoLin module: ESP8266 based NodeMCU
